# Fritzing sketch Energino (saved by Fritzing 0.7.5b)
breadboards: 1

parts:
  100k = Resistor [tolerance=±5% resistance=100k package=THT]
  -_IN_+ = Screw terminal - 2 pins [package=THT]
  10k = Resistor [tolerance=±5% resistance=10k package=THT]
  -_OUT_+ = Screw terminal - 2 pins [package=THT]
  Q1 = NPN-Transistor [package="TO92 [THT]"]
  ACS712_Low_Current = ACS712 Low Current Sensor Board v12
  1k = Resistor [tolerance=±5% resistance=1k package=THT]
  IC1 = IC, DIP package, 12 pins [chip_label=Relay spacing=300mil]
  10k_2 = Resistor [tolerance=±5% resistance=10k package=THT]
  Energino = Arduino
  D1 = Rectifier Diode [part_number=1N4001 package="300 mil [THT]"]

nets:
  N1: 100k.Pin_0, 10k.Pin_1, Energino.A1
  N2: 100k.Pin_1, -_IN_+.pin1, ACS712_Low_Current.IP+
  GND: -_IN_+.pin2, 10k.Pin_0, -_OUT_+.pin2, ACS712_Low_Current.GND, 10k_2.Pin_0, Energino.GND
  N3: -_OUT_+.pin1, IC1.pin4
  N4: Q1.B, 1k.Pin_0, 10k_2.Pin_1
  N5: Q1.C, IC1.pin12, D1.anode
  N6: ACS712_Low_Current.IP-, IC1.pin1
  5V: ACS712_Low_Current.5V, IC1.pin7, IC1.pin8, Energino.+5V, D1.cathode
  N7: ACS712_Low_Current.VO, Energino.A0
  N8: 1k.Pin_1, Energino.D2
