# Fritzing sketch EnerginoBis (saved by Fritzing 0.7.10b)
breadboards: 1

parts:
  100k = Resistor [tolerance=±5% resistance=100k package=THT]
  -_OUT_+ = Screw terminal - 2 pins [package=THT]
  10k = Resistor [tolerance=±5% resistance=10k package=THT]
  -_IN_+ = Screw terminal - 2 pins [package=THT]
  Q1 = NPN-Transistor [part_number=fdsfds package="TO92 [THT]"]
  1k = Resistor [tolerance=±5% resistance=1k package=THT]
  10k_2 = Resistor [tolerance=±5% resistance=10k package=THT]
  D1 = Rectifier Diode [part_number=1N4001 package="300 mil [THT]"]
  OMRON_G6E-134PL-ST-US = IC, DIP package, 12 pins [chip_label=IC spacing=300mil]
  Allegro_ACS712 = SO08 [chip_label=IC spacing=300mil package=SO]
  0_1uF = Ceramic Capacitor [capacitance=0.1µF package="100 mil [THT, multilayer]"]
  1k_2 = Resistor [tolerance=±5% resistance=1k package=THT]
  47k = Resistor [tolerance=±5% resistance=47k package=THT]
  47k_2 = Resistor [tolerance=±5% resistance=47k package=THT]
  OPA344 = IC, DIP package, 8 pins [chip_label=IC]
  47k_3 = Resistor [tolerance=±5% resistance=47k package=THT]
  0_1uF_2 = Ceramic Capacitor [capacitance=0.1µF package="100 mil [THT, multilayer]"]
  0_1uF_3 = Ceramic Capacitor [capacitance=0.1µF package="100 mil [THT, multilayer]"]
  0_1uF_4 = Ceramic Capacitor [capacitance=0.1µF package="100 mil [THT, multilayer]"]
  1nF = Ceramic Capacitor [capacitance=1nF package="100 mil [THT, multilayer]"]
  WIZ820io1 = WIZ820io [part_number=WIZ820io]
  Energino_v2 = Arduino

nets:
  N1: 100k.Pin_0, 10k.Pin_1, Energino_v2.A1
  N2: 100k.Pin_1, -_IN_+.pin1, OMRON_G6E-134PL-ST-US.pin10
  N3: -_OUT_+.pin1, Allegro_ACS712.1, Allegro_ACS712.2
  GND: -_OUT_+.pin2, 10k.Pin_0, -_IN_+.pin2, Q1.E, 10k_2.Pin_0, Allegro_ACS712.5, 0_1uF.1, 47k_2.Pin_0, OPA344.pin4, 0_1uF_2.1, 0_1uF_3.1, 1nF.0, WIZ820io1.GND, Energino_v2.GND
  N4: Q1.B, 1k.Pin_0, 10k_2.Pin_1
  N5: Q1.C, D1.anode, OMRON_G6E-134PL-ST-US.pin1
  N6: 1k.Pin_1, Energino_v2.D2
  5V: D1.cathode, OMRON_G6E-134PL-ST-US.pin6, Allegro_ACS712.8, 0_1uF.0, 47k.Pin_0, OPA344.pin7, 0_1uF_3.0, Energino_v2.+5V
  N7: OMRON_G6E-134PL-ST-US.pin7, Allegro_ACS712.3, Allegro_ACS712.4
  N8: Allegro_ACS712.6, 1nF.1
  N9: Allegro_ACS712.7, 1k_2.Pin_1, Energino_v2.A2
  N10: 1k_2.Pin_0, OPA344.pin2, 47k_3.Pin_1, 0_1uF_4.1
  N11: 47k.Pin_1, 47k_2.Pin_1, OPA344.pin3, 0_1uF_2.0
  N12: OPA344.pin6, 47k_3.Pin_0, 0_1uF_4.0, Energino_v2.A0
  N13: WIZ820io1.MOSI, Energino_v2.D11
  N14: WIZ820io1.SCLK, Energino_v2.D13
  N15: WIZ820io1.nSS, Energino_v2.D10
  N16: WIZ820io1.MISO, Energino_v2.D12
  VIN: WIZ820io1.VIN, Energino_v2.3V3
