# Fritzing sketch EnerginoBisMini (saved by Fritzing 0.8.0b)
breadboards: 1

parts:
  OMRON_G6E-134PL-ST-US = IC, DIP package, 12 pins [chip_label=IC spacing=300mil part_number="Omron G6E-134PL-ST-US"]
  -_IN_+ = double row male pin header, 2 pins [form="♂ (male)"]
  -_OUT_+ = double row male pin header, 2 pins [form="♂ (male)"]
  OPA344 = SO08 [chip_label=IC package=SO]
  1nF = Ceramic Capacitor [capacitance=1nF package="0805 [SMD, multilayer]"]
  47k = Resistor [tolerance=±5% resistance=47k package="0805 [SMD]"]
  0_1uF = Ceramic Capacitor [capacitance=0.1µF package="0805 [SMD, multilayer]"]
  0_1uF_2 = Ceramic Capacitor [capacitance=0.1µF package="0805 [SMD, multilayer]"]
  0_1uF_3 = Ceramic Capacitor [capacitance=0.1µF package="0805 [SMD, multilayer]"]
  1k = Resistor [tolerance=±5% resistance=1k package="0805 [SMD]"]
  0_1uF_4 = Ceramic Capacitor [capacitance=0.1µF package="0805 [SMD, multilayer]"]
  47k_2 = Resistor [tolerance=±5% resistance=47k package="0805 [SMD]"]
  Part1 = Arduino Micro (Rev3)
  10k = Resistor [tolerance=±5% resistance=10k package="0805 [SMD]"]
  100k = Resistor [tolerance=±5% resistance=100k package="0805 [SMD]"]
  Allegro_ACS712 = SO08 [chip_label=IC package=SO]
  Q1 = NPN-Transistor [package="SOT-23 [SMD]"]
  1k_2 = Resistor [tolerance=±5% resistance=1k package="0805 [SMD]"]
  10k_2 = Resistor [tolerance=±5% resistance=10k package="0805 [SMD]"]
  47k_3 = Resistor [tolerance=±5% resistance=47k package="0805 [SMD]"]

nets:
  N1: OMRON_G6E-134PL-ST-US.pin1, Q1.1
  5V: OMRON_G6E-134PL-ST-US.pin6, OPA344.7, 0_1uF.0, 0_1uF_2.0, Allegro_ACS712.8, 47k_3.Pin_0
  N2: OMRON_G6E-134PL-ST-US.pin7, -_IN_+.pin1, 100k.Pin_1
  N3: OMRON_G6E-134PL-ST-US.pin10, Allegro_ACS712.3, Allegro_ACS712.4
  GND: -_IN_+.pin2, -_OUT_+.pin2, OPA344.4, 1nF.0, 47k.Pin_0, 0_1uF.1, 0_1uF_2.1, 0_1uF_3.1, Part1.GND, 10k.Pin_0, Allegro_ACS712.5, Q1.2, 10k_2.Pin_0
  N4: -_OUT_+.pin1, Allegro_ACS712.1, Allegro_ACS712.2
  N5: OPA344.2, 1k.Pin_0, 0_1uF_4.1, 47k_2.Pin_1
  N6: OPA344.3, 47k.Pin_1, 0_1uF_3.0, 47k_3.Pin_1
  N7: OPA344.6, 0_1uF_4.0, 47k_2.Pin_0, Part1.A1
  N8: 1nF.1, Allegro_ACS712.6
  N9: 1k.Pin_1, Allegro_ACS712.7
  N10: Part1.D5_PWM, 1k_2.Pin_1
  N11: Part1.A0, 10k.Pin_1, 100k.Pin_0
  N12: Q1.0, 1k_2.Pin_0, 10k_2.Pin_1
