# Fritzing sketch EnerginoDuo (saved by Fritzing 0.7.5b)
breadboards: 1

parts:
  100k = Resistor [tolerance=±5% resistance=100k package=THT]
  10k = Resistor [tolerance=±5% resistance=10k package=THT]
  Q1 = NPN-Transistor [package="TO92 [THT]"]
  1k = Resistor [tolerance=±5% resistance=1k package=THT]
  IC1 = IC, DIP package, 12 pins [chip_label=Relay spacing=300mil]
  ACS712_Low_Current = ACS712 Low Current Sensor Board v12
  10k_2 = Resistor [tolerance=±5% resistance=10k package=THT]
  100k_2 = Resistor [tolerance=±5% resistance=100k package=THT]
  Energino_Duo_v1 = Arduino
  ACS712_Low_Current2 = ACS712 Low Current Sensor Board v12
  IC3 = IC, DIP package, 12 pins [chip_label=Relay spacing=300mil]
  D1 = Rectifier Diode [part_number=1N4001 package="300 mil [THT]"]
  I1_I2_IG = screw terminal, 3 pins
  O1_O2_OG = screw terminal, 3 pins
  Q2 = NPN-Transistor [package="TO92 [THT]"]
  D2 = Rectifier Diode [part_number=1N4001 package="300 mil [THT]"]
  1k_2 = Resistor [tolerance=±5% resistance=1k package=THT]
  10k_3 = Resistor [tolerance=±5% resistance=10k package=THT]
  10k1 = Resistor [tolerance=±5% resistance=10k package=THT]

nets (from the pcb view):
  N1: 100k.Pin_0, 10k.Pin_1, Energino_Duo_v1.A1
  N2: 100k.Pin_1, ACS712_Low_Current.IP-, I1_I2_IG.pin3
  GND: 10k.Pin_0, Q1.E, ACS712_Low_Current.GND, 10k_2.Pin_0, Energino_Duo_v1.GND, ACS712_Low_Current2.GND, I1_I2_IG.pin1, O1_O2_OG.pin1, Q2.E, 10k_3.Pin_0, 10k1.Pin_0
  N3: Q1.B, 1k.Pin_0, 10k_3.Pin_1
  N4: Q1.C, IC1.pin12, D1.anode
  N5: 1k.Pin_1, Energino_Duo_v1.D2
  N6: IC1.pin1, ACS712_Low_Current.IP+
  N7: IC1.pin4, O1_O2_OG.pin2
  5V: IC1.pin7, ACS712_Low_Current.5V, Energino_Duo_v1.+5V, ACS712_Low_Current2.5V, IC3.pin7, D1.cathode, D2.cathode
  N8: ACS712_Low_Current.VO, Energino_Duo_v1.A0
  N9: 10k_2.Pin_1, 100k_2.Pin_0, Energino_Duo_v1.A3
  N10: 100k_2.Pin_1, ACS712_Low_Current2.IP-, I1_I2_IG.pin2
  N11: Energino_Duo_v1.D3, 1k_2.Pin_1
  N12: Energino_Duo_v1.A2, ACS712_Low_Current2.VO
  N13: ACS712_Low_Current2.IP+, IC3.pin1
  N14: IC3.pin4, O1_O2_OG.pin3
  N15: IC3.pin12, Q2.C, D2.anode
  N16: Q2.B, 1k_2.Pin_0, 10k1.Pin_1
